# Fritzing sketch abzugshaube (saved by Fritzing 0.9.3b)
circuit board: 8.46667cm x 5.64444cm
breadboards: 1

parts:
  R1 = Resistor [tolerance=±5% resistance=2.50k package=THT]
  J2_(Power) = double row male pin header, 2 pins [form="♂ (male)"]
  J1_(Haube) = double row male pin header, 8 pins [form="♂ (male)"]
  U1 = ESP8266 WiFi Module [part_number=ESP8266]
  J3_(Panel) = double row male pin header, 8 pins [form="♂ (male)"]
  D1 = Diode [package=diode-1n4148]
  D2 = Diode [package=diode-1n4148]
  IC1 = '4050 Hex Buffer
  FTDI_Adapter = double row male pin header, 6 pins [form="♂ (male)"]
  U2 = mystery part, 3 pins [chip_label=Step-Down]
  Flash = Pushbutton [package=THT]
  Reset = Pushbutton [package=THT]
  C1 = Electrolytic Capacitor [capacitance=800µF package="100 mil [THT, electrolytic]"]

nets:
  N1: R1.Pin_0, J1_(Haube).pin1, J3_(Panel).pin1, IC1.B
  GND: R1.Pin_1, J2_(Power).pin2, U1.GND, U1.GPIO_15, IC1.VSS, FTDI_Adapter.pin6, U2.pin2, Flash.leg0, Reset.leg0, C1.-
  N2: J2_(Power).pin1, U2.pin3
  N3: J1_(Haube).pin2, J3_(Panel).pin2
  N4: J1_(Haube).pin3, J3_(Panel).pin3
  N5: J1_(Haube).pin4, J3_(Panel).pin4
  N6: J1_(Haube).pin5, U1.GPIO_12, J3_(Panel).pin5
  N7: J1_(Haube).pin6, U1.GPIO_14, J3_(Panel).pin6
  N8: J1_(Haube).pin7, D2.C, IC1.A
  N9: J1_(Haube).pin8, D1.C, IC1.C
  N10: U1.RXD, FTDI_Adapter.pin3
  VCC: U1.VCC, U1.CH_PD, IC1.VCC, FTDI_Adapter.pin4, U2.pin1, C1.+
  N11: U1.GPIO_0, Flash.leg1
  N12: U1.TXD, FTDI_Adapter.pin2
  N13: U1.GPIO_4, IC1.I
  N14: U1.GPIO_5, IC1.G
  N15: U1.GPIO_13, IC1.H
  N16: U1.REST, Reset.leg1
  N17: J3_(Panel).pin7, D2.A
  N18: J3_(Panel).pin8, D1.A

notes:
  Reset
  Flash

custom parts:
  ESP8266 WiFi Module: Generic WiFi Module based on the ESP8266 with onboard PCB antenna and UART communications
