# Fritzing sketch frontpanel-abzugshaube (saved by Fritzing 0.9.3b)
breadboards: 1

parts:
  S2 = Pushbutton [package="[THT]"]
  J1_(br) = male pin header, 1 pin [form="♂ (male)"]
  J2 = male pin header, 1 pin [form="♂ (male)"]
  J3 = male pin header, 1 pin [form="♂ (male)"]
  J4 = male pin header, 1 pin [form="♂ (male)"]
  J5 = male pin header, 1 pin [form="♂ (male)"]
  J6 = male pin header, 1 pin [form="♂ (male)"]
  J7 = male pin header, 1 pin [form="♂ (male)"]
  J8 = male pin header, 1 pin [form="♂ (male)"]
  S3 = Pushbutton [package="[THT]"]
  S1 = Pushbutton [package="[THT]"]
  S4 = Pushbutton [package="[THT]"]
  S7 = Pushbutton [package="[THT]"]
  S5 = Pushbutton [package="[THT]"]
  S6 = Pushbutton [package="[THT]"]
  LED2 = LED - 5mm [color="Red (633nm)" package="5 mm [THT]"]
  LED3 = LED - 5mm [color="Red (633nm)" package="5 mm [THT]"]
  LED1 = LED - 5mm [color="Red (633nm)" package="5 mm [THT]"]
  LED4 = LED - 5mm [color="Red (633nm)" package="5 mm [THT]"]
  LED6 = LED - 5mm [color="Red (633nm)" package="5 mm [THT]"]
  LED5 = LED - 5mm [color="Red (633nm)" package="5 mm [THT]"]
  LED7 = LED - 5mm [color="Red (633nm)" package="5 mm [THT]"]

nets:
  N1: S2.Pin_1, S2.Pin_2, J1_(br).pin1, S6.Pin_1, S6.Pin_2, LED2.anode, LED6.anode
  N2: S2.Pin_4, J5.pin1, S3.Pin_4, S1.Pin_4, S4.Pin_3, S4.Pin_4
  N3: J2.pin1, S3.Pin_1, S3.Pin_2, S7.Pin_1, S7.Pin_2, LED3.anode, LED7.anode
  N4: J3.pin1, S1.Pin_1, S1.Pin_2, S5.Pin_1, S5.Pin_2, LED1.anode, LED5.anode
  N5: J4.pin1, S4.Pin_1, S4.Pin_2, LED4.anode
  N6: J6.pin1, S7.Pin_3, S7.Pin_4, S5.Pin_4, S6.Pin_4
  N7: J7.pin1, LED2.cathode, LED3.cathode, LED1.cathode, LED4.cathode
  N8: J8.pin1, LED6.cathode, LED5.cathode, LED7.cathode

notes:
  S1: Warte auf HIGH auf J1, setze J5 auf High
  LED1: Warte auf HIGH auf J1, lese HIGH/LOW auf J7
